# Fritzing sketch Wiring Diagram (saved by Fritzing 0.9.2b)
breadboards: 2

parts:
  Part1 = Arduino Mega 2560 (Rev3)
  LCD1 = LCD screen  # not connected
  Part2 = Arduino Mega 2560 (Rev3)
  U1 = Thumb Joystick [package=joystick]  # not connected
  R1 = Photocell (LDR) [package=THT]  # not connected
  LED1 = LEDs [package=led10mm]  # not connected

nets:
  N1: Part1.D19/RX1, Part2.D18/TX1
  N2: Part1.D18/TX1, Part2.D19/RX1

notes:
  Bluetooth/UART
  Laser
